# Fritzing sketch CO2_Sensor_LCD (saved by Fritzing 0.9.4)
breadboards: 1

parts:
  Part2 = Arduino Nano (Rev3.0)
  LED1 = RGB LED - (4 legs) [package="5 mm [THT]"]
  LCM1602_IIC1 = LCM1602 IIC [part_number="LCM1602 IIC" chip_label="LCM1602 IIC" package="DIP (Dual Inline) [THT]"]
  LCD1 = LCD screen
  U1 = SWITCH-SPST-2 [package=switch-spst-vertical]
  Part3 = Adafruit CCS811
  R1 = Resistor [tolerance=±5% resistance=90 package=THT]
  R2 = Resistor [tolerance=±5% resistance=90 package=THT]
  R3 = Resistor [tolerance=±5% resistance=160 package=THT]

nets:
  GND: Part2.GND, LED1.blue_cathode, LCM1602_IIC1.GND, Part3.GND, Part3.!WAKE
  N1: Part2.D9, R1.Pin_1
  N2: Part2.D10, R2.Pin_1
  N3: Part2.D11/MOSI, R3.Pin_1
  5V: Part2.5V, LCM1602_IIC1.VCC, Part3.VIN
  N4: Part2.A5, LCM1602_IIC1.SCL, Part3.SCL
  N5: Part2.A4, LCM1602_IIC1.SDA, Part3.SDA
  N6: LED1.red_cathode, R3.Pin_0
  N7: LED1.common_anode, R2.Pin_0
  N8: LED1.green_cathode, R1.Pin_0
  VSS: LCM1602_IIC1.VSS, LCD1.VSS
  VDD: LCM1602_IIC1.VDD, LCD1.VDD
  N9: LCM1602_IIC1.V0, LCD1.V0
  N10: LCM1602_IIC1.RS, LCD1.RS
  N11: LCM1602_IIC1.RW, LCD1.R/W
  N12: LCM1602_IIC1.E, LCD1.E
  N13: LCM1602_IIC1.D0, LCD1.DB0
  N14: LCM1602_IIC1.D1, LCD1.DB1
  N15: LCM1602_IIC1.D2, LCD1.DB2
  N16: LCM1602_IIC1.D3, LCD1.DB3
  N17: LCM1602_IIC1.D4, LCD1.DB4
  N18: LCM1602_IIC1.D5, LCD1.DB5
  N19: LCM1602_IIC1.D6, LCD1.DB6
  N20: LCM1602_IIC1.D7, LCD1.DB7
  N21: LCM1602_IIC1.A, LCD1.LED+
  N22: LCM1602_IIC1.K, LCD1.LED-
  N23: LCM1602_IIC1.LED_A, U1.O
  N24: LCM1602_IIC1.LED_B, U1.P

custom parts:
  LCM1602 IIC: I2C-Module to use a 1602 or 2004 LCD on with the wire.h libory Serial LCD Modul
